// Logisim project control-logic.circ as structural Verilog: 1 circuit, main circuit control_logic
module control_logic (
  input  [31:0] Instruction,
  input  BrEq,
  input  BrLt,
  output PCSel,
  output RegWEn,
  output [2:0] ImmSel,
  output BrUn,
  output ASel,
  output BSel,
  output [3:0] ALUSel,
  output MemWEn,
  output [1:0] WBSel
);

  wire add, add_on, addi, and_6_out, and_7_out, and_8_out, and_9_out, and_11_out, and_13_out, and_tun, andi,
       auipc, B_ON, beq, bge, bgeu, blt, bltu, bne, demultiplexer_1_out0, demultiplexer_1_out1,
       demultiplexer_2_out1, demultiplexer_2_out5, demultiplexer_4_out3, demultiplexer_4_out4,
       demultiplexer_4_out5, demultiplexer_4_out6, demultiplexer_4_out7, demultiplexer_5_out3,
       demultiplexer_5_out4, demultiplexer_5_out5, demultiplexer_5_out6, demultiplexer_5_out7, I_IMM_ON, jal,
       jalr, L_ON, lb, lh, lui, lw, mul, mul_on, mulh, mulh_on, mulhu, not_1_out, not_2_out, not_3_out,
       or_1_out, or_2_out, or_tun, ori, R_ON, S_ON, sb, sh, sll_on, sll_tun, slli, slli_on, slt, slti,
       sra_on, sra_tun, srai, srai_on, srl_on, srl_sra_tun, srl_tun, srli, srli_on, sub, sub_on, sw, xor_tun,
       xori;
  wire [5:0] priority_encoder_1_out;
  wire [15:14] rom_1_data;

  Comparator #(.width(7)) comparator_1 (.a(Instruction[6:0]), .b(7'b0000011), .eq(L_ON));  // open: gt, lt
  Comparator #(.width(7)) comparator_2 (.a(Instruction[6:0]), .b(7'b0110011), .eq(R_ON));  // open: gt, lt
  Comparator #(.width(7)) comparator_3 (.a(Instruction[6:0]), .b(7'b0010111), .eq(auipc));  // open: gt, lt
  Comparator #(.width(7)) comparator_4 (.a(Instruction[6:0]), .b(7'b0110111), .eq(lui));  // open: gt, lt
  Comparator #(.width(7)) comparator_5 (.a(Instruction[6:0]), .b(7'b1100111), .eq(jalr));  // open: gt, lt
  Comparator #(.width(7)) comparator_6 (.a(Instruction[6:0]), .b(7'b1101111), .eq(jal));  // open: gt, lt
  Priority_Encoder #(.select_enc(6)) priority_encoder_1 (
    .in0(add), .in1(mul), .in2(sub), .in3(sll_tun), .in4(mulh), .in5(mulhu), .in6(slt), .in7(xor_tun),
    .in8(srl_tun), .in9(sra_tun), .in10(or_tun), .in11(and_tun), .in12(lb), .in13(lh), .in14(lw),
    .in15(addi), .in16(slli), .in17(slti), .in18(xori), .in19(srli), .in20(srai), .in21(ori), .in22(andi),
    .in23(sb), .in24(sh), .in25(sw), .in26(beq), .in27(bne), .in28(blt), .in29(bge), .in30(bltu),
    .in31(bgeu), .in32(auipc), .in33(lui), .in34(jal), .in35(jalr), .in36(1'b0), .in37(1'b0), .in38(1'b0),
    .in39(1'b0), .in40(1'b0), .in41(1'b0), .in42(1'b0), .in43(1'b0), .in44(1'b0), .in45(1'b0), .in46(1'b0),
    .in47(1'b0), .in48(1'b0), .in49(1'b0), .in50(1'b0), .in51(1'b0), .in52(1'b0), .in53(1'b0), .in54(1'b0),
    .in55(1'b0), .in56(1'b0), .in57(1'b0), .in58(1'b0), .in59(1'b0), .in60(1'b0), .in61(1'b0), .in62(1'b0),
    .in63(1'b0), .out(priority_encoder_1_out), .en_in(1'b1));  // open: gs, en_out
  Comparator #(.width(7)) comparator_7 (.a(Instruction[6:0]), .b(7'b0010011), .eq(I_IMM_ON));  // open: gt, lt
  Comparator #(.width(7)) comparator_8 (.a(Instruction[6:0]), .b(7'b1100011), .eq(B_ON));  // open: gt, lt
  Comparator #(.width(7)) comparator_9 (.a(Instruction[6:0]), .b(7'b0100011), .eq(S_ON));  // open: gt, lt
  ROM #(.addrWidth(6), .dataWidth(16)) rom_1 (
    .addr(priority_encoder_1_out),
    .data({rom_1_data, WBSel, MemWEn, ALUSel, BSel, ASel, BrUn, ImmSel, RegWEn}));
  and and_1 (add, add_on, demultiplexer_1_out0);
  Demultiplexer #(.select(3)) demultiplexer_1 (
    .out0(demultiplexer_1_out0), .out1(demultiplexer_1_out1), .out2(slt), .out3(mulhu), .out4(xor_tun),
    .out5(srl_sra_tun), .out6(or_tun), .out7(and_tun), .in(R_ON), .sel(Instruction[14:12]));
  Comparator #(.width(7)) comparator_10 (.a(Instruction[31:25]), .b({7{1'b0}}), .eq(add_on));  // open: gt, lt
  Comparator #(.width(7)) comparator_11 (.a(Instruction[31:25]), .b(7'b0100000), .eq(sub_on));  // open: gt, lt
  Comparator #(.width(7)) comparator_12 (.a(Instruction[31:25]), .b(7'b0000001), .eq(mul_on));  // open: gt, lt
  Demultiplexer #(.select(3)) demultiplexer_2 (
    .out0(addi), .out1(demultiplexer_2_out1), .out2(slti), .out4(xori), .out5(demultiplexer_2_out5),
    .out6(ori), .out7(andi), .in(I_IMM_ON), .sel(Instruction[14:12]));  // open: out3
  Comparator #(.width(7)) comparator_13 (.a(Instruction[31:25]), .b({7{1'b0}}), .eq(srli_on));  // open: gt, lt
  Comparator #(.width(7)) comparator_14 (.a(Instruction[31:25]), .b(7'b0100000), .eq(srai_on));  // open: gt, lt
  and and_2 (sub, sub_on, demultiplexer_1_out0);
  and and_3 (slli, demultiplexer_2_out1, slli_on);
  not not_1 (not_1_out, BrLt);
  and and_4 (srai, srai_on, demultiplexer_2_out5);
  Comparator #(.width(7)) comparator_15 (.a(Instruction[31:25]), .b({7{1'b0}}), .eq(slli_on));  // open: gt, lt
  and and_5 (mul, mul_on, demultiplexer_1_out0);
  Comparator #(.width(7)) comparator_16 (.a(Instruction[31:25]), .b({7{1'b0}}), .eq(sll_on));  // open: gt, lt
  Comparator #(.width(7)) comparator_17 (.a(Instruction[31:25]), .b(7'b0000001), .eq(mulh_on));  // open: gt, lt
  and and_6 (and_6_out, beq, BrEq);
  not not_2 (not_2_out, BrEq);
  and and_7 (and_7_out, blt, BrLt);
  and and_8 (and_8_out, bltu, BrLt);
  and and_9 (and_9_out, bge, not_1_out);
  and and_10 (srli, srli_on, demultiplexer_2_out5);
  and and_11 (and_11_out, bne, not_2_out);
  not not_3 (not_3_out, BrLt);
  and and_12 (sll_tun, sll_on, demultiplexer_1_out1);
  and and_13 (and_13_out, bgeu, not_3_out);
  and and_14 (mulh, mulh_on, demultiplexer_1_out1);
  Comparator #(.width(7)) comparator_18 (.a(Instruction[31:25]), .b({7{1'b0}}), .eq(srl_on));  // open: gt, lt
  Comparator #(.width(7)) comparator_19 (.a(Instruction[31:25]), .b(7'b0100000), .eq(sra_on));  // open: gt, lt
  Demultiplexer #(.select(3)) demultiplexer_3 (
    .out0(beq), .out1(bne), .out4(blt), .out5(bge), .out6(bltu), .out7(bgeu), .in(B_ON),
    .sel(Instruction[14:12]));  // open: out2, out3
  and and_15 (srl_tun, srl_sra_tun, srl_on);
  and and_16 (sra_tun, srl_sra_tun, sra_on);
  or or_1 (or_1_out, and_6_out, and_11_out, and_7_out, and_8_out, and_9_out, and_13_out);
  or or_2 (or_2_out, jal, jalr);
  or or_3 (PCSel, or_1_out, or_2_out);
  Demultiplexer #(.select(3)) demultiplexer_4 (
    .out0(lb), .out1(lh), .out2(lw), .out3(demultiplexer_4_out3), .out4(demultiplexer_4_out4),
    .out5(demultiplexer_4_out5), .out6(demultiplexer_4_out6), .out7(demultiplexer_4_out7), .in(L_ON),
    .sel(Instruction[14:12]));
  Demultiplexer #(.select(3)) demultiplexer_5 (
    .out0(sb), .out1(sh), .out2(sw), .out3(demultiplexer_5_out3), .out4(demultiplexer_5_out4),
    .out5(demultiplexer_5_out5), .out6(demultiplexer_5_out6), .out7(demultiplexer_5_out7), .in(S_ON),
    .sel(Instruction[14:12]));

  // Other names for the same wires on the sheet: Funct_3[2:0] = Instruction[14:12]; Funct_7[6:0] = Instruction[31:25]

  // Notes on the sheet:
  //   INPUTS to your circuit
  //   contents of rom_1 (hex, n*v repeats v):
  //   100f 140f 160f 108f 148f 158f 110f 120f 128f 168f 130f 138f 41 41 41 1041 10c1 1141 1241 12c1 16c1
  //   1341 13c1 3842 3842 3842 4*3064 3074 3074 1067 17c7 2069 2041 2041
  //   ROM FOR CONTROL LOGIC
  //   DON'T CHANGE THE LOCATIONS OF THE INPUTS AND OUTPUTS!
  //   This is only if you choose to do the ROM option
  //   OUTPUT from your circuit
  //   Reminder: If using ROM, use combinational logic for PCSel
endmodule
